# Fritzing sketch fruit_sums_diagram (saved by Fritzing 0.9.3b)
breadboards: 1

parts:
  S1 = Pushbutton [package="[THT]"]
  LED1 = LED - 5mm [color="Red (633nm)" package="5 mm [THT]"]
  R1 = Resistor [tolerance=±5% resistance=220 package=THT]
  R2 = Resistor [tolerance=±5% resistance=330 package=THT]
  Raspberry_Pi_2 = Raspberry Pi B+

nets:
  N1: S1.Pin_1, S1.Pin_2, R1.Pin_1
  N2: S1.Pin_3, S1.Pin_4, Raspberry_Pi_2.GPIO15
  N3: LED1.cathode, R2.Pin_1
  N4: LED1.anode, Raspberry_Pi_2.GPIO18
  N5: R1.Pin_0, Raspberry_Pi_2.3v3
  N6: R2.Pin_0, Raspberry_Pi_2.GND
